# Fritzing sketch RotarySwitch-FM-radio (saved by Fritzing 0.9.3b)

parts:
  Pro_Mini = Arduino Pro Mini v13
  R1 = Resistor [tolerance=±5% resistance=220 package=THT]
  R2 = Resistor [tolerance=±5% resistance=220 package=THT]
  RDA5807M = RDA5807M-RRD102 [package="DIP (Dual Inline) [THT]"]
  volume = Rotary Potentiometer (Large) [maximum_resistance=100kΩ package=THT]
  SP1 = SPEAKER [package=pcb_mount_speaker]
  20K = Resistor [tolerance=±5% resistance=220 package=THT]
  10K = Resistor [tolerance=±5% resistance=220 package=THT]
  2200 = Resistor [tolerance=±5% resistance=220 package=THT]
  3300 = Resistor [tolerance=±5% resistance=220 package=THT]
  3300_2 = Resistor [tolerance=±5% resistance=220 package=THT]
  4700 = Resistor [tolerance=±5% resistance=220 package=THT]
  6800 = Resistor [tolerance=±5% resistance=220 package=THT]
  20K_2 = Resistor [tolerance=±5% resistance=220 package=THT]
  47K = Resistor [tolerance=±5% resistance=220 package=THT]
  220K = Resistor [tolerance=±5% resistance=220 package=THT]
  3300_3 = Resistor [tolerance=±5% resistance=220 package=THT]
  2200_2 = Resistor [tolerance=±5% resistance=220 package=THT]
  20K_3 = Resistor [tolerance=±5% resistance=220 package=THT]
  20K_4 = Resistor [tolerance=±5% resistance=220 package=THT]
  on/off = SWITCH_SPDT [package=kps-1290]
  Mono_Amplifier = Mono amp
  charger = Adafruit USB LiIon/LiPoly Charger [part_number="Adafruit #259"]
  U1 = LIPO-1000mAh [package=lipo-1000]  # not connected
  Rotary_0_to_9 = Rotary_Switch_12x1
  6800_2 = Resistor [tolerance=±5% resistance=220 package=THT]
  4700_2 = Resistor [tolerance=±5% resistance=220 package=THT]
  3300_4 = Resistor [tolerance=±5% resistance=220 package=THT]
  3300_5 = Resistor [tolerance=±5% resistance=220 package=THT]
  2200_3 = Resistor [tolerance=±5% resistance=220 package=THT]
  220K1 = Resistor [tolerance=±5% resistance=220 package=THT]
  47K1 = Resistor [tolerance=±5% resistance=220 package=THT]
  20K1 = Resistor [tolerance=±5% resistance=220 package=THT]
  10K1 = Resistor [tolerance=±5% resistance=220 package=THT]
  Rotary_0_to_9_2 = Rotary_Switch_12x1
  Rotary_8_9_10 = Rotary_Switch_12x1
  D1 = SOLAR-IXYS [package=solarbit-12x1]
  D2 = Schottky Diode [part_number=1N5817 package="300 mil [THT]"]
  D3 = Schottky Diode [part_number=1N5817 package="300 mil [THT]"]  # not connected

nets:
  N1: Pro_Mini.A4, RDA5807M.DATA
  N2: Pro_Mini.A5, RDA5807M.SCLK
  N3: Pro_Mini.GND, 2200_2.Pin_1, 2200_3.Pin_1, Rotary_0_to_9_2.1, Rotary_8_9_10.1
  VCC: Pro_Mini.VCC, 20K.Pin_1, 20K_3.Pin_1, 20K_4.Pin_1, on/off.O, Mono_Amplifier.VCC, D2.anode
  N4: Pro_Mini.A2, 20K_3.Pin_0, Rotary_0_to_9.0
  N5: Pro_Mini.A1, 20K.Pin_0, Rotary_0_to_9_2.0
  N6: Pro_Mini.A0, 20K_4.Pin_0, Rotary_8_9_10.0
  N7: R1.Pin_0, R2.Pin_0, volume.leg2
  N8: R1.Pin_1, RDA5807M.LOUT
  N9: R2.Pin_1, RDA5807M.ROUT
  N10: volume.leg1, Mono_Amplifier.IN+, Mono_Amplifier.GND
  N11: volume.wiper, Mono_Amplifier.IN-
  N12: SP1.+, Mono_Amplifier.OUT+
  N13: SP1.-, Mono_Amplifier.OUT-
  N14: 10K.Pin_0, 6800.Pin_0, Rotary_0_to_9.6
  N15: 10K.Pin_1, 20K_2.Pin_0, Rotary_0_to_9.7
  N16: 2200.Pin_0, 3300.Pin_1, Rotary_0_to_9.2
  N17: 2200.Pin_1, Rotary_0_to_9.1
  N18: 3300.Pin_0, 3300_2.Pin_1, Rotary_0_to_9.3
  N19: 3300_2.Pin_0, 4700.Pin_1, Rotary_0_to_9.4
  N20: 4700.Pin_0, 6800.Pin_1, Rotary_0_to_9.5
  N21: 20K_2.Pin_1, 47K.Pin_0, Rotary_0_to_9.8
  N22: 47K.Pin_1, 220K.Pin_0, Rotary_0_to_9.9
  N23: 220K.Pin_1, Rotary_0_to_9.10
  N24: 3300_3.Pin_0, Rotary_8_9_10.3
  N25: 3300_3.Pin_1, 2200_2.Pin_0, Rotary_8_9_10.2
  N26: charger.GND, D1.C
  N27: charger.5.0V, D1.A
  N28: 6800_2.Pin_0, 10K1.Pin_0, Rotary_0_to_9_2.6
  N29: 6800_2.Pin_1, 4700_2.Pin_0, Rotary_0_to_9_2.5
  N30: 4700_2.Pin_1, 3300_4.Pin_0, Rotary_0_to_9_2.4
  N31: 3300_4.Pin_1, 3300_5.Pin_0, Rotary_0_to_9_2.3
  N32: 3300_5.Pin_1, 2200_3.Pin_0, Rotary_0_to_9_2.2
  N33: 220K1.Pin_0, 47K1.Pin_1, Rotary_0_to_9_2.9
  N34: 220K1.Pin_1, Rotary_0_to_9_2.10
  N35: 47K1.Pin_0, 20K1.Pin_1, Rotary_0_to_9_2.8
  N36: 20K1.Pin_0, 10K1.Pin_1, Rotary_0_to_9_2.7

custom parts:
  RDA5807M-RRD102: RRD102 board with RDA5807M chip and quartz
  Adafruit USB LiIon/LiPoly Charger: This is a Lithium Ion and Lithium Polymer battery charger based on the MCP73833. It uses a USB mini-B for connection to any computer or 'USB wall adapter'. Charging is performed in three stages: first a preconditioning charge, then a constant-current fast charge and finally a constant-voltage trickle charge to keep the battery topped-up. The fast-charge current is 500mA by default, but is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
  Rotary_Switch_12x1: Rotary Switch 12 position 1 pole
